# Fritzing sketch ArduinoNano-Single_L293D-v0 (saved by Fritzing 0.9.3b)
breadboards: 1

parts:
  S1 = H-Bridge with L298N
  J1 = Peltier Element
  J2 = Peltier Element
  Part1 = Arduino Nano (Rev3.0)
  Power_plug1 = Power plug

nets:
  12V: S1.12V, Power_plug1.VCC
  GND: S1.GND, Power_plug1.GND
  5V: S1.5V, Part1.5V
  N1: S1.ENA, Part1.D2
  N2: S1.IN1, Part1.D3
  N3: S1.IN2, Part1.D4
  N4: S1.IN3, Part1.D5
  N5: S1.IN4, Part1.D6
  N6: S1.ENB, Part1.D7
  N7: S1.M1-01, J2.pin2
  N8: S1.M1-02, J2.pin1
  N9: S1.M2-01, J1.pin2
  N10: S1.M2-02, J1.pin1

custom parts:
  H-Bridge with L298N: h-bridge
